// Logisim project full_arithmatic_with_decoder_selector.circ as structural Verilog: 5 circuits, main circuit main
module main (
  input  [2:0] in_1,
  input  [7:0] Ain,
  input  [7:0] Bin,
  output out_4,
  output out_5,
  output out_6,
  output out_7,
  output out_8,
  output out_9,
  output out_10,
  output [7:0] out
);

  wire n3bit_arithmaticselector_1_out_2;

  _8bit_AddSubtract u_8bit_addsubtract_1 (
    .Cout(out_10), .Sub(n3bit_arithmaticselector_1_out_2), .Ain(Ain), .Bin(Bin), .out_5(out));
  _3bit_ArithmaticSelector u_3bit_arithmaticselector_1 (
    .in_1(in_1), .out_2(n3bit_arithmaticselector_1_out_2), .out_3(out_4), .out_4(out_5), .out_5(out_6),
    .out_6(out_7), .out_7(out_8), .out_8(out_9));

  // Notes on the sheet:
  //   000 == Addition
  //   001 == Subtraction
  //   010 == Multiplication
  //   011 == Division
  //   100 == Modulus
  //   101 == Equal To
  //   110 == Greater Than
  //   111 == Less Than
endmodule

module _3bit_ArithmaticSelector (
  input  [2:0] in_1,
  output out_2,
  output out_3,
  output out_4,
  output out_5,
  output out_6,
  output out_7,
  output out_8
);

  wire and_1_out, and_2_out;

  and and_1 (and_1_out, ~in_1[2], ~in_1[1], ~in_1[0]);  // AND_Gate
  and and_2 (and_2_out, ~in_1[2], ~in_1[1], in_1[0]);  // AND_Gate
  or or_1 (out_2, ~and_1_out, and_2_out);  // OR_Gate
  and and_3 (out_4, ~in_1[2], in_1[1], in_1[0]);  // AND_Gate
  and and_4 (out_3, ~in_1[2], in_1[1], ~in_1[0]);  // AND_Gate
  and and_5 (out_7, in_1[2], in_1[1], ~in_1[0]);  // AND_Gate
  and and_6 (out_6, in_1[2], ~in_1[1], in_1[0]);  // AND_Gate
  and and_7 (out_5, in_1[2], ~in_1[1], ~in_1[0]);  // AND_Gate
  and and_8 (out_8, in_1[2], in_1[1], in_1[0]);

  // Notes on the sheet:
  //   000 == Addition
  //   011 == Division
  //   100 == Modulus
  //   101 == Equal To
  //   001 == Subtraction
  //   010 == Multiplication
  //   110 == Greater Than
  //   111 == Less Than
endmodule

module _1bit_AddSubtract (
  input  Ain,
  input  Sub,
  input  Bin,
  input  Cin,
  output Cout,
  output out
);

  wire and_1_out, and_2_out, or_1_out;

  and and_1 (and_1_out, Sub, ~Bin);  // AND_Gate
  and and_2 (and_2_out, Bin, ~Sub);  // AND_Gate
  or or_1 (or_1_out, and_1_out, and_2_out);
  Adder #(.width(1)) adder_1 (.a(Ain), .b(or_1_out), .out(out), .cin(Cin), .cout(Cout));
endmodule

module _8bit_AddSubtract (
  input  [7:0] Ain,
  input  [7:0] Bin,
  input  Sub,
  output Cout,
  output [7:0] out_5
);

  wire n1bit_addsubtract_2_cout, n1bit_addsubtract_3_cout, n1bit_addsubtract_4_cout,
       n1bit_addsubtract_5_cout, n1bit_addsubtract_6_cout, n1bit_addsubtract_7_cout, n1bit_addsubtract_8_cout;

  _1bit_AddSubtract u_1bit_addsubtract_1 (
    .Cout(Cout), .Sub(Sub), .Ain(Ain[7]), .Bin(Bin[7]), .out(out_5[7]), .Cin(n1bit_addsubtract_2_cout));
  _1bit_AddSubtract u_1bit_addsubtract_2 (
    .Cout(n1bit_addsubtract_2_cout), .Sub(Sub), .Ain(Ain[6]), .Bin(Bin[6]), .out(out_5[6]),
    .Cin(n1bit_addsubtract_3_cout));
  _1bit_AddSubtract u_1bit_addsubtract_3 (
    .Cout(n1bit_addsubtract_3_cout), .Sub(Sub), .Ain(Ain[5]), .Bin(Bin[5]), .out(out_5[5]),
    .Cin(n1bit_addsubtract_4_cout));
  _1bit_AddSubtract u_1bit_addsubtract_4 (
    .Cout(n1bit_addsubtract_4_cout), .Sub(Sub), .Ain(Ain[4]), .Bin(Bin[4]), .out(out_5[4]),
    .Cin(n1bit_addsubtract_5_cout));
  _1bit_AddSubtract u_1bit_addsubtract_5 (
    .Cout(n1bit_addsubtract_5_cout), .Sub(Sub), .Ain(Ain[3]), .Bin(Bin[3]), .out(out_5[3]),
    .Cin(n1bit_addsubtract_6_cout));
  _1bit_AddSubtract u_1bit_addsubtract_6 (
    .Cout(n1bit_addsubtract_6_cout), .Sub(Sub), .Ain(Ain[2]), .Bin(Bin[2]), .out(out_5[2]),
    .Cin(n1bit_addsubtract_7_cout));
  _1bit_AddSubtract u_1bit_addsubtract_7 (
    .Cout(n1bit_addsubtract_7_cout), .Sub(Sub), .Ain(Ain[1]), .Bin(Bin[1]), .out(out_5[1]),
    .Cin(n1bit_addsubtract_8_cout));
  _1bit_AddSubtract u_1bit_addsubtract_8 (
    .Cout(n1bit_addsubtract_8_cout), .Sub(Sub), .Ain(Ain[0]), .Bin(Bin[0]), .out(out_5[0]), .Cin(Sub));
endmodule

module _8bit_EqualTo (
  input  [7:0] in_1,
  input  [7:0] in_2,
  output out_3
);

  wire [7:0] xnor_1_out;

  assign xnor_1_out = ~(in_1 ^ in_2);  // XNOR_Gate xnor_1, 8 bits wide
  and and_1 (out_3, xnor_1_out[7], xnor_1_out[6], xnor_1_out[5], xnor_1_out[4], xnor_1_out[3], xnor_1_out[2], xnor_1_out[1], xnor_1_out[0]);
endmodule
