// Logisim project not_nor_or_nand_and.circ as structural Verilog: 1 circuit, main circuit main
module main (
  input  Input,
  input  Input_2,
  input  Input_3,
  input  A,
  input  A_2,
  input  in_6,
  input  B,
  input  B_2,
  input  A_3,
  input  _1in,
  input  _2in,
  input  _1in_2,
  input  _2in_2,
  input  _1in_3,
  input  _2in_3,
  input  _3in,
  input  A_4,
  input  _3in_2,
  input  A_5,
  input  A_6,
  input  B_3,
  input  _3in_3,
  input  B_4,
  input  B_5,
  input  C,
  input  Input_4,
  input  A_7,
  output _1out,
  output _1out_2,
  output _1out_3,
  output _1out_4,
  output _1out_5,
  output _1out_6,
  output _1out_7
);

  wire transistor_6_out, transistor_7_out, transistor_12_out, transistor_15_out, transistor_18_out,
       transistor_21_out, transistor_22_out, transistor_27_out, transistor_30_out, transistor_31_out;

  Transistor transistor_1 (.in(Input_3), .out(_1out), .gate(A_3));
  Transistor #(.\type ("n")) transistor_2 (.in(1'b0), .out(_1out), .gate(A_3));
  Transistor transistor_3 (.in(_1in), .out(_1out_4), .gate(A_4));
  Transistor transistor_4 (.in(_2in), .out(_1out_4), .gate(B_3));
  Transistor #(.\type ("n")) transistor_5 (.in(transistor_6_out), .out(_1out_4), .gate(A_4));
  Transistor #(.\type ("n")) transistor_6 (.in(1'b0), .out(transistor_6_out), .gate(B_3));
  Transistor transistor_7 (.in(Input_4), .out(transistor_7_out), .gate(A_7));
  Transistor transistor_8 (.in(A_7), .out(_1out_7), .gate(Input_4));
  Transistor #(.\type ("n")) transistor_9 (.in(1'b0), .out(transistor_7_out), .gate(A_7));
  Transistor #(.\type ("n")) transistor_10 (.in(1'b0), .out(_1out_2), .gate(B_2));
  Transistor #(.\type ("n")) transistor_11 (.in(transistor_7_out), .out(_1out_7), .gate(Input_4));
  Transistor transistor_12 (.in(Input_2), .out(transistor_12_out), .gate(A_2));
  Transistor transistor_13 (.in(transistor_12_out), .out(_1out_2), .gate(B_2));
  Transistor #(.\type ("n")) transistor_14 (.in(1'b0), .out(_1out_2), .gate(A_2));
  Transistor transistor_15 (.in(_1in_2), .out(transistor_15_out), .gate(A_5));
  Transistor transistor_16 (.in(_2in_2), .out(transistor_15_out), .gate(B_4));
  Transistor #(.\type ("n")) transistor_17 (.in(transistor_18_out), .out(transistor_15_out), .gate(A_5));
  Transistor #(.\type ("n")) transistor_18 (.in(1'b0), .out(transistor_18_out), .gate(B_4));
  Transistor transistor_19 (.in(_3in_2), .out(_1out_5), .gate(transistor_15_out));
  Transistor #(.\type ("n")) transistor_20 (.in(1'b0), .out(_1out_5), .gate(transistor_15_out));
  Transistor transistor_21 (.in(Input), .out(transistor_21_out), .gate(A));
  Transistor transistor_22 (.in(transistor_21_out), .out(transistor_22_out), .gate(B));
  Transistor #(.\type ("n")) transistor_23 (.in(1'b0), .out(transistor_22_out), .gate(B));
  Transistor transistor_24 (.in(in_6), .out(_1out_3), .gate(transistor_22_out));
  Transistor #(.\type ("n")) transistor_25 (.in(1'b0), .out(_1out_3), .gate(transistor_22_out));
  Transistor #(.\type ("n")) transistor_26 (.in(1'b0), .out(transistor_22_out), .gate(A));
  Transistor transistor_27 (.in(_2in_3), .out(transistor_27_out), .gate(B_5));
  Transistor transistor_28 (.in(_1in_3), .out(transistor_27_out), .gate(A_6));
  Transistor #(.\type ("n")) transistor_29 (.in(transistor_30_out), .out(transistor_27_out), .gate(A_6));
  Transistor #(.\type ("n")) transistor_30 (.in(transistor_31_out), .out(transistor_30_out), .gate(B_5));
  Transistor #(.\type ("n")) transistor_31 (.in(1'b0), .out(transistor_31_out), .gate(C));
  Transistor transistor_32 (.in(_3in), .out(transistor_27_out), .gate(C));
  Transistor transistor_33 (.in(_3in_3), .out(_1out_6), .gate(transistor_27_out));
  Transistor #(.\type ("n")) transistor_34 (.in(1'b0), .out(_1out_6), .gate(transistor_27_out));

  // Notes on the sheet:
  //   NOT Logic Gate
  //   NAND Logic Gate
  //   Custom Double-NOT Inverter
  //   NOR Logic Gate
  //   AND Logic Gate
  //   OR Logic Gate
  //   3bit AND Logic Gate
endmodule
