// Logisim project von_neumann_circuit.circ as structural Verilog: 9 circuits, main circuit main
module main (
  input  [3:0] in_1,
  input  [7:0] Ain,
  input  [7:0] Bin,
  output out_4,
  output out_5,
  output out_6,
  output out_7,
  output out_8,
  output out_9,
  output out_10,
  output out_11,
  output out_12,
  output out_13,
  output out_14,
  output out_15,
  output out_16,
  output out_17,
  output out_18,
  output [7:0] out
);

  wire addsubtractselector_1_out_3, n3bit_arithmaticselector_1_out_16, n3bit_arithmaticselector_1_out_17;

  _8bit_AddSubtract u_8bit_addsubtract_1 (
    .Cout(out_18), .Sub(addsubtractselector_1_out_3), .Ain(Ain), .Bin(Bin), .out_5(out));
  AddSubtractSelector addsubtractselector_1 (
    .in_1(n3bit_arithmaticselector_1_out_16), .in_2(n3bit_arithmaticselector_1_out_17),
    .out_3(addsubtractselector_1_out_3));
  _3bit_ArithmaticSelector u_3bit_arithmaticselector_1 (
    .in_1(in_1), .out_2(out_4), .out_3(out_5), .out_4(out_6), .out_5(out_7), .out_6(out_8), .out_7(out_9),
    .out_8(out_10), .out_9(out_11), .out_10(out_12), .out_11(out_13), .out_12(out_14), .out_13(out_15),
    .out_14(out_16), .out_15(out_17), .out_16(n3bit_arithmaticselector_1_out_16),
    .out_17(n3bit_arithmaticselector_1_out_17));

  // Notes on the sheet:
  //   0000 == Addition
  //   0001 == Subtraction
  //   0010 == Multiplication
  //   0011 == Division
  //   0100 == Modulus
  //   0101 == Equal To
  //   0110 == Greater Than
  //   0111 == Less Than
  //   1000 == FREE
  //   1001 == FREE
  //   1010 == FREE
  //   1011 == FREE
  //   1100 == FREE
  //   1101 == FREE
  //   1110 == FREE
  //   1111 == FREE
endmodule

module _3bit_ArithmaticSelector (
  input  [3:0] in_1,
  output out_2,
  output out_3,
  output out_4,
  output out_5,
  output out_6,
  output out_7,
  output out_8,
  output out_9,
  output out_10,
  output out_11,
  output out_12,
  output out_13,
  output out_14,
  output out_15,
  output out_16,
  output out_17
);

  and and_1 (out_3, in_1[3], in_1[2], in_1[1], ~in_1[0]);  // AND_Gate
  and and_2 (out_2, in_1[3], in_1[2], in_1[1], in_1[0]);
  and and_3 (out_4, in_1[3], in_1[2], ~in_1[1], in_1[0]);  // AND_Gate
  and and_4 (out_5, in_1[3], in_1[2], ~in_1[1], ~in_1[0]);  // AND_Gate
  and and_5 (out_6, in_1[3], ~in_1[2], in_1[1], in_1[0]);  // AND_Gate
  and and_6 (out_8, in_1[3], ~in_1[2], ~in_1[1], in_1[0]);  // AND_Gate
  and and_7 (out_7, in_1[3], ~in_1[2], in_1[1], ~in_1[0]);  // AND_Gate
  and and_8 (out_9, in_1[3], ~in_1[2], ~in_1[1], ~in_1[0]);  // AND_Gate
  and and_9 (out_11, ~in_1[3], in_1[2], in_1[1], ~in_1[0]);  // AND_Gate
  and and_10 (out_10, ~in_1[3], in_1[2], in_1[1], in_1[0]);  // AND_Gate
  and and_11 (out_12, ~in_1[3], in_1[2], ~in_1[1], in_1[0]);  // AND_Gate
  and and_12 (out_13, ~in_1[3], in_1[2], ~in_1[1], ~in_1[0]);  // AND_Gate
  and and_13 (out_14, ~in_1[3], ~in_1[2], in_1[1], in_1[0]);  // AND_Gate
  and and_14 (out_16, ~in_1[3], ~in_1[2], ~in_1[1], in_1[0]);  // AND_Gate
  and and_15 (out_15, ~in_1[3], ~in_1[2], in_1[1], ~in_1[0]);  // AND_Gate
  and and_16 (out_17, ~in_1[3], ~in_1[2], ~in_1[1], ~in_1[0]);  // AND_Gate

  // Notes on the sheet:
  //   0000 == Addition
  //   0001 == Subtraction
  //   0010 == Multiplication
  //   0011 == Division
  //   0100 == Modulus
  //   0101 == Equal To
  //   0110 == Greater Than
  //   0111 == Less Than
  //   1000 == FREE
  //   1001 == FREE
  //   1010 == FREE
  //   1011 == FREE
  //   1100 == FREE
  //   1101 == FREE
  //   1110 == FREE
  //   1111 == FREE
endmodule

module _1bit_AddSubtract (
  input  Ain,
  input  Sub,
  input  Bin,
  input  Cin,
  output Cout,
  output out
);

  wire and_1_out, and_2_out, or_1_out;

  and and_1 (and_1_out, Bin, ~Sub);  // AND_Gate
  and and_2 (and_2_out, Sub, ~Bin);  // AND_Gate
  or or_1 (or_1_out, and_2_out, and_1_out);
  Adder #(.width(1)) adder_1 (.a(Ain), .b(or_1_out), .out(out), .cin(Cin), .cout(Cout));
endmodule

module _8bit_AddSubtract (
  input  [7:0] Ain,
  input  [7:0] Bin,
  input  Sub,
  output Cout,
  output [7:0] out_5
);

  wire n1bit_addsubtract_2_cout, n1bit_addsubtract_3_cout, n1bit_addsubtract_4_cout,
       n1bit_addsubtract_5_cout, n1bit_addsubtract_6_cout, n1bit_addsubtract_7_cout, n1bit_addsubtract_8_cout;

  _1bit_AddSubtract u_1bit_addsubtract_1 (
    .Cout(Cout), .Sub(Sub), .Ain(Ain[7]), .Bin(Bin[7]), .out(out_5[7]), .Cin(n1bit_addsubtract_2_cout));
  _1bit_AddSubtract u_1bit_addsubtract_2 (
    .Cout(n1bit_addsubtract_2_cout), .Sub(Sub), .Ain(Ain[6]), .Bin(Bin[6]), .out(out_5[6]),
    .Cin(n1bit_addsubtract_3_cout));
  _1bit_AddSubtract u_1bit_addsubtract_3 (
    .Cout(n1bit_addsubtract_3_cout), .Sub(Sub), .Ain(Ain[5]), .Bin(Bin[5]), .out(out_5[5]),
    .Cin(n1bit_addsubtract_5_cout));
  _1bit_AddSubtract u_1bit_addsubtract_4 (
    .Cout(n1bit_addsubtract_4_cout), .Sub(Sub), .Ain(Ain[3]), .Bin(Bin[3]), .out(out_5[3]),
    .Cin(n1bit_addsubtract_6_cout));
  _1bit_AddSubtract u_1bit_addsubtract_5 (
    .Cout(n1bit_addsubtract_5_cout), .Sub(Sub), .Ain(Ain[4]), .Bin(Bin[4]), .out(out_5[4]),
    .Cin(n1bit_addsubtract_4_cout));
  _1bit_AddSubtract u_1bit_addsubtract_6 (
    .Cout(n1bit_addsubtract_6_cout), .Sub(Sub), .Ain(Ain[2]), .Bin(Bin[2]), .out(out_5[2]),
    .Cin(n1bit_addsubtract_7_cout));
  _1bit_AddSubtract u_1bit_addsubtract_7 (
    .Cout(n1bit_addsubtract_7_cout), .Sub(Sub), .Ain(Ain[1]), .Bin(Bin[1]), .out(out_5[1]),
    .Cin(n1bit_addsubtract_8_cout));
  _1bit_AddSubtract u_1bit_addsubtract_8 (
    .Cout(n1bit_addsubtract_8_cout), .Sub(Sub), .Ain(Ain[0]), .Bin(Bin[0]), .out(out_5[0]), .Cin(Sub));
endmodule

module _8bit_EqualTo (
  input  [7:0] in_1,
  input  [7:0] in_2,
  output out_3
);

  wire [7:0] xnor_1_out;

  assign xnor_1_out = ~(in_1 ^ in_2);  // XNOR_Gate xnor_1, 8 bits wide
  and and_1 (out_3, xnor_1_out[7], xnor_1_out[6], xnor_1_out[5], xnor_1_out[4], xnor_1_out[3], xnor_1_out[2], xnor_1_out[1], xnor_1_out[0]);
endmodule

module AddSubtractSelector (
  input  in_1,
  input  in_2,
  output out_3
);

  and and_1 (out_3, in_1, ~in_2);  // AND_Gate
endmodule

module _1by16bit_Registry (
  input  [15:0] Din,
  input  WEin,
  output out_3,
  output out_4,
  output out_5,
  output out_6,
  output out_7,
  output out_8,
  output out_9,
  output out_10,
  output out_11,
  output out_12,
  output out_13,
  output out_14,
  output out_15,
  output out_16,
  output out_17,
  output out_18
);

  wire nand_1_out, nand_2_out, nand_3_out, nand_4_out, nand_5_out, nand_7_out, nand_9_out, nand_10_out,
       nand_12_out, nand_13_out, nand_14_out, nand_15_out, nand_16_out, nand_17_out, nand_19_out,
       nand_20_out, nand_22_out, nand_23_out, nand_25_out, nand_26_out, nand_28_out, nand_29_out,
       nand_30_out, nand_31_out, nand_32_out, nand_34_out, nand_35_out, nand_36_out, nand_38_out,
       nand_39_out, nand_41_out, nand_42_out, nand_43_out, nand_45_out, nand_46_out, nand_47_out,
       nand_48_out, nand_50_out, nand_51_out, nand_52_out, nand_53_out, nand_55_out, nand_57_out,
       nand_58_out, nand_60_out, nand_61_out, nand_62_out, nand_63_out;

  nand nand_1 (nand_1_out, WEin, ~Din[15]);  // NAND_Gate
  nand nand_2 (nand_2_out, nand_1_out, out_3);
  nand nand_3 (nand_3_out, Din[15], WEin);
  nand nand_4 (nand_4_out, WEin, ~Din[14]);  // NAND_Gate
  nand nand_5 (nand_5_out, nand_4_out, out_4);
  nand nand_6 (out_3, nand_2_out, nand_3_out);
  nand nand_7 (nand_7_out, Din[14], WEin);
  nand nand_8 (out_4, nand_5_out, nand_7_out);
  nand nand_9 (nand_9_out, WEin, ~Din[13]);  // NAND_Gate
  nand nand_10 (nand_10_out, Din[13], WEin);
  nand nand_11 (out_5, nand_12_out, nand_10_out);
  nand nand_12 (nand_12_out, nand_9_out, out_5);
  nand nand_13 (nand_13_out, WEin, ~Din[12]);  // NAND_Gate
  nand nand_14 (nand_14_out, nand_13_out, out_6);
  nand nand_15 (nand_15_out, WEin, ~Din[11]);  // NAND_Gate
  nand nand_16 (nand_16_out, Din[12], WEin);
  nand nand_17 (nand_17_out, nand_15_out, out_7);
  nand nand_18 (out_6, nand_14_out, nand_16_out);
  nand nand_19 (nand_19_out, WEin, ~Din[10]);  // NAND_Gate
  nand nand_20 (nand_20_out, Din[11], WEin);
  nand nand_21 (out_7, nand_17_out, nand_20_out);
  nand nand_22 (nand_22_out, nand_19_out, out_8);
  nand nand_23 (nand_23_out, Din[10], WEin);
  nand nand_24 (out_8, nand_22_out, nand_23_out);
  nand nand_25 (nand_25_out, WEin, ~Din[9]);  // NAND_Gate
  nand nand_26 (nand_26_out, Din[9], WEin);
  nand nand_27 (out_9, nand_28_out, nand_26_out);
  nand nand_28 (nand_28_out, nand_25_out, out_9);
  nand nand_29 (nand_29_out, WEin, ~Din[8]);  // NAND_Gate
  nand nand_30 (nand_30_out, nand_29_out, out_10);
  nand nand_31 (nand_31_out, WEin, ~Din[7]);  // NAND_Gate
  nand nand_32 (nand_32_out, Din[8], WEin);
  nand nand_33 (out_10, nand_30_out, nand_32_out);
  nand nand_34 (nand_34_out, nand_31_out, out_11);
  nand nand_35 (nand_35_out, WEin, ~Din[6]);  // NAND_Gate
  nand nand_36 (nand_36_out, Din[7], WEin);
  nand nand_37 (out_11, nand_34_out, nand_36_out);
  nand nand_38 (nand_38_out, nand_35_out, out_12);
  nand nand_39 (nand_39_out, Din[6], WEin);
  nand nand_40 (out_12, nand_38_out, nand_39_out);
  nand nand_41 (nand_41_out, Din[5], WEin);
  nand nand_42 (nand_42_out, WEin, ~Din[5]);  // NAND_Gate
  nand nand_43 (nand_43_out, nand_42_out, out_13);
  nand nand_44 (out_13, nand_43_out, nand_41_out);
  nand nand_45 (nand_45_out, WEin, ~Din[4]);  // NAND_Gate
  nand nand_46 (nand_46_out, nand_45_out, out_14);
  nand nand_47 (nand_47_out, Din[4], WEin);
  nand nand_48 (nand_48_out, WEin, ~Din[3]);  // NAND_Gate
  nand nand_49 (out_14, nand_46_out, nand_47_out);
  nand nand_50 (nand_50_out, nand_48_out, out_15);
  nand nand_51 (nand_51_out, WEin, ~Din[2]);  // NAND_Gate
  nand nand_52 (nand_52_out, Din[3], WEin);
  nand nand_53 (nand_53_out, nand_51_out, out_16);
  nand nand_54 (out_15, nand_50_out, nand_52_out);
  nand nand_55 (nand_55_out, Din[2], WEin);
  nand nand_56 (out_16, nand_53_out, nand_55_out);
  nand nand_57 (nand_57_out, WEin, ~Din[1]);  // NAND_Gate
  nand nand_58 (nand_58_out, Din[1], WEin);
  nand nand_59 (out_17, nand_60_out, nand_58_out);
  nand nand_60 (nand_60_out, nand_57_out, out_17);
  nand nand_61 (nand_61_out, WEin, ~Din[0]);  // NAND_Gate
  nand nand_62 (nand_62_out, nand_61_out, out_18);
  nand nand_63 (nand_63_out, Din[0], WEin);
  nand nand_64 (out_18, nand_62_out, nand_63_out);
endmodule

module _2_3by8bit_Registry_MAR (
  input  WE,
  input  [2:0] AddrSel,
  input  [15:0] Din,
  output [15:0] Dout
);

  wire and_1_out, and_2_out, and_3_out, and_4_out, and_5_out, and_6_out, and_7_out, and_8_out, and_9_out,
       and_10_out, and_11_out, and_12_out, and_13_out, and_14_out, and_15_out, and_16_out,
       n1by16bit_registry_1_out_3, n1by16bit_registry_1_out_4, n1by16bit_registry_1_out_5,
       n1by16bit_registry_1_out_6, n1by16bit_registry_1_out_7, n1by16bit_registry_1_out_8,
       n1by16bit_registry_1_out_9, n1by16bit_registry_1_out_10, n1by16bit_registry_1_out_11,
       n1by16bit_registry_1_out_12, n1by16bit_registry_1_out_13, n1by16bit_registry_1_out_14,
       n1by16bit_registry_1_out_15, n1by16bit_registry_1_out_16, n1by16bit_registry_1_out_17,
       n1by16bit_registry_1_out_18, n1by16bit_registry_2_out_3, n1by16bit_registry_2_out_4,
       n1by16bit_registry_2_out_5, n1by16bit_registry_2_out_6, n1by16bit_registry_2_out_7,
       n1by16bit_registry_2_out_8, n1by16bit_registry_2_out_9, n1by16bit_registry_2_out_10,
       n1by16bit_registry_2_out_11, n1by16bit_registry_2_out_12, n1by16bit_registry_2_out_13,
       n1by16bit_registry_2_out_14, n1by16bit_registry_2_out_15, n1by16bit_registry_2_out_16,
       n1by16bit_registry_2_out_17, n1by16bit_registry_2_out_18, n1by16bit_registry_3_out_3,
       n1by16bit_registry_3_out_4, n1by16bit_registry_3_out_5, n1by16bit_registry_3_out_6,
       n1by16bit_registry_3_out_7, n1by16bit_registry_3_out_8, n1by16bit_registry_3_out_9,
       n1by16bit_registry_3_out_10, n1by16bit_registry_3_out_11, n1by16bit_registry_3_out_12,
       n1by16bit_registry_3_out_13, n1by16bit_registry_3_out_14, n1by16bit_registry_3_out_15,
       n1by16bit_registry_3_out_16, n1by16bit_registry_3_out_17, n1by16bit_registry_3_out_18,
       n1by16bit_registry_4_out_3, n1by16bit_registry_4_out_4, n1by16bit_registry_4_out_5,
       n1by16bit_registry_4_out_6, n1by16bit_registry_4_out_7, n1by16bit_registry_4_out_8,
       n1by16bit_registry_4_out_9, n1by16bit_registry_4_out_10, n1by16bit_registry_4_out_11,
       n1by16bit_registry_4_out_12, n1by16bit_registry_4_out_13, n1by16bit_registry_4_out_14,
       n1by16bit_registry_4_out_15, n1by16bit_registry_4_out_16, n1by16bit_registry_4_out_17,
       n1by16bit_registry_4_out_18, n1by16bit_registry_5_out_3, n1by16bit_registry_5_out_4,
       n1by16bit_registry_5_out_5, n1by16bit_registry_5_out_6, n1by16bit_registry_5_out_7,
       n1by16bit_registry_5_out_8, n1by16bit_registry_5_out_9, n1by16bit_registry_5_out_10,
       n1by16bit_registry_5_out_11, n1by16bit_registry_5_out_12, n1by16bit_registry_5_out_13,
       n1by16bit_registry_5_out_14, n1by16bit_registry_5_out_15, n1by16bit_registry_5_out_16,
       n1by16bit_registry_5_out_17, n1by16bit_registry_5_out_18, n1by16bit_registry_6_out_3,
       n1by16bit_registry_6_out_4, n1by16bit_registry_6_out_5, n1by16bit_registry_6_out_6,
       n1by16bit_registry_6_out_7, n1by16bit_registry_6_out_8, n1by16bit_registry_6_out_9,
       n1by16bit_registry_6_out_10, n1by16bit_registry_6_out_11, n1by16bit_registry_6_out_12,
       n1by16bit_registry_6_out_13, n1by16bit_registry_6_out_14, n1by16bit_registry_6_out_15,
       n1by16bit_registry_6_out_16, n1by16bit_registry_6_out_17, n1by16bit_registry_6_out_18,
       n1by16bit_registry_7_out_3, n1by16bit_registry_7_out_4, n1by16bit_registry_7_out_5,
       n1by16bit_registry_7_out_6, n1by16bit_registry_7_out_7, n1by16bit_registry_7_out_8,
       n1by16bit_registry_7_out_9, n1by16bit_registry_7_out_10, n1by16bit_registry_7_out_11,
       n1by16bit_registry_7_out_12, n1by16bit_registry_7_out_13, n1by16bit_registry_7_out_14,
       n1by16bit_registry_7_out_15, n1by16bit_registry_7_out_16, n1by16bit_registry_7_out_17,
       n1by16bit_registry_7_out_18, n1by16bit_registry_8_out_3, n1by16bit_registry_8_out_4,
       n1by16bit_registry_8_out_5, n1by16bit_registry_8_out_6, n1by16bit_registry_8_out_7,
       n1by16bit_registry_8_out_8, n1by16bit_registry_8_out_9, n1by16bit_registry_8_out_10,
       n1by16bit_registry_8_out_11, n1by16bit_registry_8_out_12, n1by16bit_registry_8_out_13,
       n1by16bit_registry_8_out_14, n1by16bit_registry_8_out_15, n1by16bit_registry_8_out_16,
       n1by16bit_registry_8_out_17, n1by16bit_registry_8_out_18;
  wire [15:0] regselector_mux_1_out_18, regselector_mux_2_out_18, regselector_mux_3_out_18,
       regselector_mux_4_out_18, regselector_mux_5_out_18, regselector_mux_6_out_18,
       regselector_mux_7_out_18, regselector_mux_8_out_18;

  and and_1 (and_1_out, ~AddrSel[0], ~AddrSel[1], ~AddrSel[2]);  // AND_Gate
  and and_2 (and_2_out, AddrSel[0], ~AddrSel[1], ~AddrSel[2]);  // AND_Gate
  and and_3 (and_3_out, ~AddrSel[0], AddrSel[1], ~AddrSel[2]);  // AND_Gate
  and and_4 (and_4_out, AddrSel[0], AddrSel[1], ~AddrSel[2]);  // AND_Gate
  and and_5 (and_5_out, AddrSel[0], AddrSel[1], ~AddrSel[2]);  // AND_Gate
  and and_6 (and_6_out, AddrSel[0], ~AddrSel[1], AddrSel[2]);  // AND_Gate
  and and_7 (and_7_out, ~AddrSel[0], AddrSel[1], AddrSel[2]);  // AND_Gate
  and and_8 (and_8_out, AddrSel[0], AddrSel[1], AddrSel[2]);
  and and_9 (and_9_out, and_1_out, WE);
  and and_10 (and_10_out, and_2_out, WE);
  and and_11 (and_11_out, and_3_out, WE);
  and and_12 (and_12_out, and_4_out, WE);
  and and_13 (and_13_out, and_5_out, WE);
  and and_14 (and_14_out, and_6_out, WE);
  and and_15 (and_15_out, and_7_out, WE);
  and and_16 (and_16_out, and_8_out, WE);
  RegSelector_Mux regselector_mux_1 (
    .in_17(and_1_out), .in_1(n1by16bit_registry_1_out_3), .in_2(n1by16bit_registry_1_out_4),
    .in_3(n1by16bit_registry_1_out_5), .in_4(n1by16bit_registry_1_out_6), .in_5(n1by16bit_registry_1_out_7),
    .in_6(n1by16bit_registry_1_out_8), .in_7(n1by16bit_registry_1_out_9), .in_8(n1by16bit_registry_1_out_10),
    .in_9(n1by16bit_registry_1_out_11), .in_10(n1by16bit_registry_1_out_12),
    .in_11(n1by16bit_registry_1_out_13), .in_12(n1by16bit_registry_1_out_14),
    .in_13(n1by16bit_registry_1_out_15), .in_14(n1by16bit_registry_1_out_16),
    .in_15(n1by16bit_registry_1_out_17), .in_16(n1by16bit_registry_1_out_18),
    .out_18(regselector_mux_1_out_18));
  RegSelector_Mux regselector_mux_2 (
    .in_17(and_2_out), .in_1(n1by16bit_registry_2_out_3), .in_2(n1by16bit_registry_2_out_4),
    .in_3(n1by16bit_registry_2_out_5), .in_4(n1by16bit_registry_2_out_6), .in_5(n1by16bit_registry_2_out_7),
    .in_6(n1by16bit_registry_2_out_8), .in_7(n1by16bit_registry_2_out_9), .in_8(n1by16bit_registry_2_out_10),
    .in_9(n1by16bit_registry_2_out_11), .in_10(n1by16bit_registry_2_out_12),
    .in_11(n1by16bit_registry_2_out_13), .in_12(n1by16bit_registry_2_out_14),
    .in_13(n1by16bit_registry_2_out_15), .in_14(n1by16bit_registry_2_out_16),
    .in_15(n1by16bit_registry_2_out_17), .in_16(n1by16bit_registry_2_out_18),
    .out_18(regselector_mux_2_out_18));
  RegSelector_Mux regselector_mux_3 (
    .in_17(and_3_out), .in_1(n1by16bit_registry_3_out_3), .in_2(n1by16bit_registry_3_out_4),
    .in_3(n1by16bit_registry_3_out_5), .in_4(n1by16bit_registry_3_out_6), .in_5(n1by16bit_registry_3_out_7),
    .in_6(n1by16bit_registry_3_out_8), .in_7(n1by16bit_registry_3_out_9), .in_8(n1by16bit_registry_3_out_10),
    .in_9(n1by16bit_registry_3_out_11), .in_10(n1by16bit_registry_3_out_12),
    .in_11(n1by16bit_registry_3_out_13), .in_12(n1by16bit_registry_3_out_14),
    .in_13(n1by16bit_registry_3_out_15), .in_14(n1by16bit_registry_3_out_16),
    .in_15(n1by16bit_registry_3_out_17), .in_16(n1by16bit_registry_3_out_18),
    .out_18(regselector_mux_3_out_18));
  RegSelector_Mux regselector_mux_4 (
    .in_17(and_4_out), .in_1(n1by16bit_registry_4_out_3), .in_2(n1by16bit_registry_4_out_4),
    .in_3(n1by16bit_registry_4_out_5), .in_4(n1by16bit_registry_4_out_6), .in_5(n1by16bit_registry_4_out_7),
    .in_6(n1by16bit_registry_4_out_8), .in_7(n1by16bit_registry_4_out_9), .in_8(n1by16bit_registry_4_out_10),
    .in_9(n1by16bit_registry_4_out_11), .in_10(n1by16bit_registry_4_out_12),
    .in_11(n1by16bit_registry_4_out_13), .in_12(n1by16bit_registry_4_out_14),
    .in_13(n1by16bit_registry_4_out_15), .in_14(n1by16bit_registry_4_out_16),
    .in_15(n1by16bit_registry_4_out_17), .in_16(n1by16bit_registry_4_out_18),
    .out_18(regselector_mux_4_out_18));
  RegSelector_Mux regselector_mux_5 (
    .in_17(and_5_out), .in_1(n1by16bit_registry_5_out_3), .in_2(n1by16bit_registry_5_out_4),
    .in_3(n1by16bit_registry_5_out_5), .in_4(n1by16bit_registry_5_out_6), .in_5(n1by16bit_registry_5_out_7),
    .in_6(n1by16bit_registry_5_out_8), .in_7(n1by16bit_registry_5_out_9), .in_8(n1by16bit_registry_5_out_10),
    .in_9(n1by16bit_registry_5_out_11), .in_10(n1by16bit_registry_5_out_12),
    .in_11(n1by16bit_registry_5_out_13), .in_12(n1by16bit_registry_5_out_14),
    .in_13(n1by16bit_registry_5_out_15), .in_14(n1by16bit_registry_5_out_16),
    .in_15(n1by16bit_registry_5_out_17), .in_16(n1by16bit_registry_5_out_18),
    .out_18(regselector_mux_5_out_18));
  RegSelector_Mux regselector_mux_6 (
    .in_17(and_6_out), .in_1(n1by16bit_registry_6_out_3), .in_2(n1by16bit_registry_6_out_4),
    .in_3(n1by16bit_registry_6_out_5), .in_4(n1by16bit_registry_6_out_6), .in_5(n1by16bit_registry_6_out_7),
    .in_6(n1by16bit_registry_6_out_8), .in_7(n1by16bit_registry_6_out_9), .in_8(n1by16bit_registry_6_out_10),
    .in_9(n1by16bit_registry_6_out_11), .in_10(n1by16bit_registry_6_out_12),
    .in_11(n1by16bit_registry_6_out_13), .in_12(n1by16bit_registry_6_out_14),
    .in_13(n1by16bit_registry_6_out_15), .in_14(n1by16bit_registry_6_out_16),
    .in_15(n1by16bit_registry_6_out_17), .in_16(n1by16bit_registry_6_out_18),
    .out_18(regselector_mux_6_out_18));
  RegSelector_Mux regselector_mux_7 (
    .in_17(and_7_out), .in_1(n1by16bit_registry_7_out_3), .in_2(n1by16bit_registry_7_out_4),
    .in_3(n1by16bit_registry_7_out_5), .in_4(n1by16bit_registry_7_out_6), .in_5(n1by16bit_registry_7_out_7),
    .in_6(n1by16bit_registry_7_out_8), .in_7(n1by16bit_registry_7_out_9), .in_8(n1by16bit_registry_7_out_10),
    .in_9(n1by16bit_registry_7_out_11), .in_10(n1by16bit_registry_7_out_12),
    .in_11(n1by16bit_registry_7_out_13), .in_12(n1by16bit_registry_7_out_14),
    .in_13(n1by16bit_registry_7_out_15), .in_14(n1by16bit_registry_7_out_16),
    .in_15(n1by16bit_registry_7_out_17), .in_16(n1by16bit_registry_7_out_18),
    .out_18(regselector_mux_7_out_18));
  RegSelector_Mux regselector_mux_8 (
    .in_17(and_8_out), .in_1(n1by16bit_registry_8_out_3), .in_2(n1by16bit_registry_8_out_4),
    .in_3(n1by16bit_registry_8_out_5), .in_4(n1by16bit_registry_8_out_6), .in_5(n1by16bit_registry_8_out_7),
    .in_6(n1by16bit_registry_8_out_8), .in_7(n1by16bit_registry_8_out_9), .in_8(n1by16bit_registry_8_out_10),
    .in_9(n1by16bit_registry_8_out_11), .in_10(n1by16bit_registry_8_out_12),
    .in_11(n1by16bit_registry_8_out_13), .in_12(n1by16bit_registry_8_out_14),
    .in_13(n1by16bit_registry_8_out_15), .in_14(n1by16bit_registry_8_out_16),
    .in_15(n1by16bit_registry_8_out_17), .in_16(n1by16bit_registry_8_out_18),
    .out_18(regselector_mux_8_out_18));
  _1by16bit_Registry u_1by16bit_registry_1 (
    .WEin(and_9_out), .Din(Din), .out_3(n1by16bit_registry_1_out_3), .out_4(n1by16bit_registry_1_out_4),
    .out_5(n1by16bit_registry_1_out_5), .out_6(n1by16bit_registry_1_out_6),
    .out_7(n1by16bit_registry_1_out_7), .out_8(n1by16bit_registry_1_out_8),
    .out_9(n1by16bit_registry_1_out_9), .out_10(n1by16bit_registry_1_out_10),
    .out_11(n1by16bit_registry_1_out_11), .out_12(n1by16bit_registry_1_out_12),
    .out_13(n1by16bit_registry_1_out_13), .out_14(n1by16bit_registry_1_out_14),
    .out_15(n1by16bit_registry_1_out_15), .out_16(n1by16bit_registry_1_out_16),
    .out_17(n1by16bit_registry_1_out_17), .out_18(n1by16bit_registry_1_out_18));
  _1by16bit_Registry u_1by16bit_registry_2 (
    .WEin(and_10_out), .Din(Din), .out_3(n1by16bit_registry_2_out_3), .out_4(n1by16bit_registry_2_out_4),
    .out_5(n1by16bit_registry_2_out_5), .out_6(n1by16bit_registry_2_out_6),
    .out_7(n1by16bit_registry_2_out_7), .out_8(n1by16bit_registry_2_out_8),
    .out_9(n1by16bit_registry_2_out_9), .out_10(n1by16bit_registry_2_out_10),
    .out_11(n1by16bit_registry_2_out_11), .out_12(n1by16bit_registry_2_out_12),
    .out_13(n1by16bit_registry_2_out_13), .out_14(n1by16bit_registry_2_out_14),
    .out_15(n1by16bit_registry_2_out_15), .out_16(n1by16bit_registry_2_out_16),
    .out_17(n1by16bit_registry_2_out_17), .out_18(n1by16bit_registry_2_out_18));
  _1by16bit_Registry u_1by16bit_registry_3 (
    .WEin(and_11_out), .Din(Din), .out_3(n1by16bit_registry_3_out_3), .out_4(n1by16bit_registry_3_out_4),
    .out_5(n1by16bit_registry_3_out_5), .out_6(n1by16bit_registry_3_out_6),
    .out_7(n1by16bit_registry_3_out_7), .out_8(n1by16bit_registry_3_out_8),
    .out_9(n1by16bit_registry_3_out_9), .out_10(n1by16bit_registry_3_out_10),
    .out_11(n1by16bit_registry_3_out_11), .out_12(n1by16bit_registry_3_out_12),
    .out_13(n1by16bit_registry_3_out_13), .out_14(n1by16bit_registry_3_out_14),
    .out_15(n1by16bit_registry_3_out_15), .out_16(n1by16bit_registry_3_out_16),
    .out_17(n1by16bit_registry_3_out_17), .out_18(n1by16bit_registry_3_out_18));
  _1by16bit_Registry u_1by16bit_registry_4 (
    .WEin(and_12_out), .Din(Din), .out_3(n1by16bit_registry_4_out_3), .out_4(n1by16bit_registry_4_out_4),
    .out_5(n1by16bit_registry_4_out_5), .out_6(n1by16bit_registry_4_out_6),
    .out_7(n1by16bit_registry_4_out_7), .out_8(n1by16bit_registry_4_out_8),
    .out_9(n1by16bit_registry_4_out_9), .out_10(n1by16bit_registry_4_out_10),
    .out_11(n1by16bit_registry_4_out_11), .out_12(n1by16bit_registry_4_out_12),
    .out_13(n1by16bit_registry_4_out_13), .out_14(n1by16bit_registry_4_out_14),
    .out_15(n1by16bit_registry_4_out_15), .out_16(n1by16bit_registry_4_out_16),
    .out_17(n1by16bit_registry_4_out_17), .out_18(n1by16bit_registry_4_out_18));
  _1by16bit_Registry u_1by16bit_registry_5 (
    .WEin(and_13_out), .Din(Din), .out_3(n1by16bit_registry_5_out_3), .out_4(n1by16bit_registry_5_out_4),
    .out_5(n1by16bit_registry_5_out_5), .out_6(n1by16bit_registry_5_out_6),
    .out_7(n1by16bit_registry_5_out_7), .out_8(n1by16bit_registry_5_out_8),
    .out_9(n1by16bit_registry_5_out_9), .out_10(n1by16bit_registry_5_out_10),
    .out_11(n1by16bit_registry_5_out_11), .out_12(n1by16bit_registry_5_out_12),
    .out_13(n1by16bit_registry_5_out_13), .out_14(n1by16bit_registry_5_out_14),
    .out_15(n1by16bit_registry_5_out_15), .out_16(n1by16bit_registry_5_out_16),
    .out_17(n1by16bit_registry_5_out_17), .out_18(n1by16bit_registry_5_out_18));
  _1by16bit_Registry u_1by16bit_registry_6 (
    .WEin(and_14_out), .Din(Din), .out_3(n1by16bit_registry_6_out_3), .out_4(n1by16bit_registry_6_out_4),
    .out_5(n1by16bit_registry_6_out_5), .out_6(n1by16bit_registry_6_out_6),
    .out_7(n1by16bit_registry_6_out_7), .out_8(n1by16bit_registry_6_out_8),
    .out_9(n1by16bit_registry_6_out_9), .out_10(n1by16bit_registry_6_out_10),
    .out_11(n1by16bit_registry_6_out_11), .out_12(n1by16bit_registry_6_out_12),
    .out_13(n1by16bit_registry_6_out_13), .out_14(n1by16bit_registry_6_out_14),
    .out_15(n1by16bit_registry_6_out_15), .out_16(n1by16bit_registry_6_out_16),
    .out_17(n1by16bit_registry_6_out_17), .out_18(n1by16bit_registry_6_out_18));
  _1by16bit_Registry u_1by16bit_registry_7 (
    .WEin(and_15_out), .Din(Din), .out_3(n1by16bit_registry_7_out_3), .out_4(n1by16bit_registry_7_out_4),
    .out_5(n1by16bit_registry_7_out_5), .out_6(n1by16bit_registry_7_out_6),
    .out_7(n1by16bit_registry_7_out_7), .out_8(n1by16bit_registry_7_out_8),
    .out_9(n1by16bit_registry_7_out_9), .out_10(n1by16bit_registry_7_out_10),
    .out_11(n1by16bit_registry_7_out_11), .out_12(n1by16bit_registry_7_out_12),
    .out_13(n1by16bit_registry_7_out_13), .out_14(n1by16bit_registry_7_out_14),
    .out_15(n1by16bit_registry_7_out_15), .out_16(n1by16bit_registry_7_out_16),
    .out_17(n1by16bit_registry_7_out_17), .out_18(n1by16bit_registry_7_out_18));
  _1by16bit_Registry u_1by16bit_registry_8 (
    .WEin(and_16_out), .Din(Din), .out_3(n1by16bit_registry_8_out_3), .out_4(n1by16bit_registry_8_out_4),
    .out_5(n1by16bit_registry_8_out_5), .out_6(n1by16bit_registry_8_out_6),
    .out_7(n1by16bit_registry_8_out_7), .out_8(n1by16bit_registry_8_out_8),
    .out_9(n1by16bit_registry_8_out_9), .out_10(n1by16bit_registry_8_out_10),
    .out_11(n1by16bit_registry_8_out_11), .out_12(n1by16bit_registry_8_out_12),
    .out_13(n1by16bit_registry_8_out_13), .out_14(n1by16bit_registry_8_out_14),
    .out_15(n1by16bit_registry_8_out_15), .out_16(n1by16bit_registry_8_out_16),
    .out_17(n1by16bit_registry_8_out_17), .out_18(n1by16bit_registry_8_out_18));
  assign Dout = regselector_mux_1_out_18 | regselector_mux_2_out_18 | regselector_mux_3_out_18 | regselector_mux_4_out_18 | regselector_mux_5_out_18 | regselector_mux_6_out_18 | regselector_mux_7_out_18 | regselector_mux_8_out_18;  // OR_Gate or_1, 16 bits wide
endmodule

module RegSelector_Mux (
  input  in_1,
  input  in_2,
  input  in_3,
  input  in_4,
  input  in_5,
  input  in_6,
  input  in_7,
  input  in_8,
  input  in_9,
  input  in_10,
  input  in_11,
  input  in_12,
  input  in_13,
  input  in_14,
  input  in_15,
  input  in_16,
  input  in_17,
  output [15:0] out_18
);

  and and_1 (out_18[14], in_17, in_2);
  and and_2 (out_18[15], in_17, in_1);
  and and_3 (out_18[13], in_17, in_3);
  and and_4 (out_18[11], in_17, in_5);
  and and_5 (out_18[12], in_17, in_4);
  and and_6 (out_18[9], in_17, in_7);
  and and_7 (out_18[10], in_17, in_6);
  and and_8 (out_18[6], in_17, in_10);
  and and_9 (out_18[8], in_17, in_8);
  and and_10 (out_18[7], in_17, in_9);
  and and_11 (out_18[4], in_17, in_12);
  and and_12 (out_18[5], in_17, in_11);
  and and_13 (out_18[3], in_17, in_13);
  and and_14 (out_18[2], in_17, in_14);
  and and_15 (out_18[1], in_17, in_15);
  and and_16 (out_18[0], in_17, in_16);
endmodule
